# Fritzing sketch BreadBoard (saved by Fritzing 0.9.2b)
circuit board: 8.54226cm x 5.61924cm
breadboards: 1

parts:
  Part1 = Arduino Nano (Rev3.0)
  R1 = Resistor [tolerance=±5% resistance=220 package=THT]
  R2 = Resistor [tolerance=±5% resistance=10k package=THT]
  U1 = LCD-16X2 [package=lcd-16x2]
  R4 = TRIMPOT [package=3362u-2]

nets:
  GND: Part1.GND, U1.VSS, U1.R_W, U1.K, R4.CW
  N1: Part1.D2, U1.DB7
  N2: Part1.D3, U1.DB6
  N3: Part1.D4, U1.DB5
  N4: Part1.D5, U1.DB4
  N5: Part1.D8, R2.Pin_1
  N6: Part1.D11/MOSI, U1.E
  N7: Part1.D12/MISO, U1.RS
  5V: Part1.5V, R1.Pin_1, R2.Pin_0, U1.VDD, R4.CCW
  N8: R1.Pin_0, U1.A
  N9: U1.VO, R4.WIPER
